# Fritzing sketch CASA0016_smart_clay_timer (saved by Fritzing 1.0.1rc)
breadboards: 1

parts:
  Part1 = Adafruit MLX90640 Thermal Camera [part_number="Adafruit #4407"]
  DHT1 = DHT22 Humidity and Temperature Sensor
  HC-SR04_Sensor_1 = HC-SR04 Ultrasonic Distance Sensor
  Part2 = Adafruit Feather HUZZAH ESP8266 [part_number="Adafruit #2821"]
  R1 = Resistor [tolerance=±5% resistance=10k package="2512 [SMD]"]
  R2 = Resistor [tolerance=±5% resistance=10k package="2512 [SMD]"]
  R3 = Resistor [tolerance=±5% resistance=10k package="2512 [SMD]"]
  Part3 = NeoPixel Stick [part_number=1426]

nets:
  GND: Part1.GND, DHT1.GND, HC-SR04_Sensor_1.GND, Part2.GND, R2.Pin_0, Part3.GND
  N1: Part1.SDA, Part2.GPIO4/SDA
  VCC: Part1.VCC, DHT1.VDD, Part2.3.3V, R3.Pin_0
  N2: Part1.SCL, Part2.GPIO5/SCL
  N3: DHT1.DATA, Part2.GPIO2, R3.Pin_1
  VCC_2: HC-SR04_Sensor_1.VCC, Part2.VBUS, Part3.+5V
  N4: HC-SR04_Sensor_1.TRIG, Part2.GPIO15
  N5: HC-SR04_Sensor_1.ECHO, R1.Pin_0
  N6: Part2.GPIO14/SCK, Part3.DATAIN
  N7: Part2.GPIO13/MOSI, R1.Pin_1, R2.Pin_1

custom parts:
  Adafruit MLX90640 Thermal Camera: You can now add affordable heat-vision to your project and with an Adafruit MLX90640 Thermal Camera Breakout. This sensor contains a 24x32 array of IR thermal sensors. When connected to your microcontroller (or Raspberry Pi) it will return an array of 768 individual infrared temperature readings over I2C. It's like those fancy thermal cameras, but compact and simple enough for easy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
  Adafruit Feather HUZZAH ESP8266: his is the Adafruit Feather HUZZAH ESP8266 - our take on an 'all-in-one' ESP8266 WiFi development board with built in USB and battery charging. Its an ESP8266 WiFi module with all the extras you need, ready to rock! We have other boards in the Feather family, check'em out here. At the Feather HUZZAH's heart is an ESP8266 WiFi microcontroller clocked at 80 MHz and at 3.3V logic. This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
  NeoPixel Stick: Make your own little LED strip arrangement with this stick of NeoPixel LEDs. We crammed 8 of the tiny 5050 (5mm x 5mm) smart RGB LEDs onto a PCB with mounting holes and a chainable design. Use only one microcontroller pin to control as many as you can chain together! Each LED is addressable as the driver chip is inside the LED. Each one has ~18mA constant current drive so the color will be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
